# Fritzing sketch Connetction (saved by Fritzing 0.9.3b)
breadboards: 1

parts:
  U1 = GAS_SENSOR [package=mq-3]
  LED1 = smd LED [color="Red (633nm)" package="0603 [SMD]"]
  LED2 = smd LED [color="Green (555nm)" package="0603 [SMD]"]
  Part1 = Arduino Uno (Rev3) - ICSP
  R2 = Resistor [tolerance=±5% resistance=220 package="0805 [SMD]"]
  R3 = Resistor [tolerance=±5% resistance=220 package="0805 [SMD]"]
  J1 = Piezo Speaker

nets (from the breadboard view):
  N1: U1.B1, Part1.VIN
  N2: U1.A1, LED1.cathode, LED2.cathode, Part1.GND, J1.pin1
  N3: LED1.anode, R2.Pin_0
  N4: LED2.anode, R3.Pin_0
  N5: Part1.D8, R2.Pin_1
  N6: Part1.D4, R3.Pin_1
  N7: Part1.D7, J1.pin2

// code stored in the sketch: GAS_DETECTOR.ino
//Reserve A1 pin for gas sensor and name it as gas
int gas = A1;
//Reserve pin 4 for green led and name it as G_LED
int G_LED = 4;
//Reserve pin 7 for piezo buzzer and name it as Buzzer
int Buzzer = 7;
//Reserve pin 8 for red led and named it R_LED
int R_LED = 8;

// Define a variable val that stores the analog reading from A1 pin
int val;
//Initialize the max threshold as 300
int MAX = 300;

//Setup the sensors and actuator in arduino uno
void setup() {
  Serial.begin(9600);
  pinMode(gas ,INPUT);
  pinMode(R_LED ,OUTPUT);
  pinMode(G_LED ,OUTPUT);
  pinMode(Buzzer ,OUTPUT);
}

//Loop to check gas leakage
void loop() {
  val = analogRead(A1);
  if (val >= MAX) {
    digitalWrite(R_LED ,HIGH);
    digitalWrite(Buzzer ,HIGH);
    digitalWrite(G_LED ,LOW);
    Serial.println(val);
    Serial.println("GAS LEAKAGE DETECTED");
  }
  else {
    digitalWrite(R_LED ,LOW);
    digitalWrite(Buzzer ,LOW);
    digitalWrite(G_LED ,HIGH);
    Serial.println(val);
  }
}
